# Fritzing sketch MysteryMachine (saved by Fritzing 0.9.6b)
circuit board: 10cm x 16cm
breadboards: 1

parts:
  Part1 = Arduino Uno (Rev3)
  LED2_1 = LED - 5mm [color="Red (633nm)" current=0.030 package="5 mm [THT]"]
  LED2_2 = LED - 5mm [color="Yellow (595nm)" current=0.030 package="5 mm [THT]"]
  RH2 = Resistor [tolerance=±5% resistance=1M power=0.25 package=THT]
  RHM = Resistor [tolerance=±5% resistance=1M power=0.25 package=THT]
  RH1 = Resistor [tolerance=±5% resistance=1M power=0.25 package=THT]
  LED2_3 = LED - 5mm [color="Green (570nm)" current=0.030 package="5 mm [THT]"]
  R2 = Resistor [tolerance=±5% resistance=220 power=0.25 package=THT]
  LED1_1 = LED - 5mm [color="Red (633nm)" current=0.030 package="5 mm [THT]"]
  LED1_2 = LED - 5mm [color="Yellow (595nm)" current=0.030 package="5 mm [THT]"]
  LED1_3 = LED - 5mm [color="Green (555nm)" current=0.030 package="5 mm [THT]"]
  LEDM_3 = LED - 5mm [color="Red (633nm)" current=0.030 package="5 mm [THT]"]
  LEDM_2 = LED - 5mm [color="Red (633nm)" current=0.030 package="5 mm [THT]"]
  LEDM_1 = LED - 5mm [color="Red (633nm)" current=0.030 package="5 mm [THT]"]
  RM = Resistor [tolerance=±5% resistance=220 power=0.25 package=THT]
  R1 = Resistor [tolerance=±5% resistance=220 power=0.25 package=THT]
  RS2 = Resistor [tolerance=±5% resistance=1k power=0.25 package=THT]
  Touch2 = Resistor [tolerance=±5% resistance=0 power=0.25 package=THT]
  RSM = Resistor [tolerance=±5% resistance=1k power=0.25 package=THT]
  TouchMid1 = Resistor [tolerance=±5% resistance=0 power=0.25 package=THT]
  RS1 = Resistor [tolerance=±5% resistance=1k power=0.25 package=THT]
  Touch1 = Resistor [tolerance=±5% resistance=0 power=0.25 package=THT]

nets:
  N1: Part1.A0, LEDM_1.anode
  N2: Part1.A1, LEDM_2.anode
  N3: Part1.A2, LEDM_3.anode
  N4: Part1.A4/SDA, RHM.Pin_1, RSM.Pin_0
  N5: Part1.A5/SCL, RHM.Pin_0
  N6: Part1.D8, LED1_3.anode
  N7: Part1.D9_PWM, LED2_1.anode
  N8: Part1.D10_PWM/SS, LED2_2.anode
  N9: Part1.D11_PWM/MOSI, LED2_3.anode
  N10: Part1.GND, R2.Pin_0, RM.Pin_0, R1.Pin_0
  N11: Part1.D2, RH1.Pin_1, RS1.Pin_0
  N12: Part1.D3_PWM, RH1.Pin_0
  N13: Part1.D4, RH2.Pin_0, RS2.Pin_0
  N14: Part1.D5_PWM, RH2.Pin_1
  N15: Part1.D6_PWM, LED1_1.anode
  N16: Part1.D7, LED1_2.anode
  N17: LED2_1.cathode, LED2_2.cathode, LED2_3.cathode, R2.Pin_1
  N18: LED1_1.cathode, LED1_2.cathode, LED1_3.cathode, R1.Pin_1
  N19: LEDM_3.cathode, LEDM_2.cathode, LEDM_1.cathode, RM.Pin_1
  N20: RS2.Pin_1, Touch2.Pin_1
  N21: RSM.Pin_1, TouchMid1.Pin_0
  N22: RS1.Pin_1, Touch1.Pin_0
