# Fritzing sketch MysteryMachineStandalone (saved by Fritzing 0.8.7b)
circuit board: 5cm x 15cm
breadboards: 1

parts:
  LED2_1 = LED - 5mm [color="Red (633nm)" package="5 mm [THT]"]
  LED2_2 = LED - 5mm [color="Yellow (595nm)" package="5 mm [THT]"]
  LED2_3 = LED - 5mm [color="Green (570nm)" package="5 mm [THT]"]
  RLEDsTop = Resistor [tolerance=±5% resistance=220 package=THT]
  LED1_1 = LED - 5mm [color="Red (633nm)" package="5 mm [THT]"]
  LED1_2 = LED - 5mm [color="Yellow (595nm)" package="5 mm [THT]"]
  LED1_3 = LED - 5mm [color="Green (555nm)" package="5 mm [THT]"]
  LEDM_3 = LED - 5mm [color="Red (633nm)" package="5 mm [THT]"]
  LEDM_2 = LED - 5mm [color="Red (633nm)" package="5 mm [THT]"]
  LEDM_1 = LED - 5mm [color="Red (633nm)" package="5 mm [THT]"]
  RLedsMid = Resistor [tolerance=±5% resistance=220 package=THT]
  RLEDsBottom = Resistor [tolerance=±5% resistance=220 package=THT]
  U2 = atmega328 [package=dip]
  C4 = Capacitor [package=cap-pth-small2]
  C5 = Capacitor [package=cap-pth-small2]
  Y2 = CRYSTAL [package=crystal-smd-10.5x4.8-2pin]
  VCC = Battery
  TouchMid1 = Resistor [tolerance=±5% resistance=0 package=THT]
  RHMid = Resistor [tolerance=±5% resistance=1k package=THT]
  RSMid = Resistor [tolerance=±5% resistance=1M package=THT]
  RHTop = Resistor [tolerance=±5% resistance=1k package=THT]
  RSTop = Resistor [tolerance=±5% resistance=1M package=THT]
  TouchTop = Resistor [tolerance=±5% resistance=0 package=THT]
  RHBottom = Resistor [tolerance=±5% resistance=1k package=THT]
  RSBottom = Resistor [tolerance=±5% resistance=1M package=THT]
  TouchBottom = Resistor [tolerance=±5% resistance=0 package=THT]

nets:
  N1: LED2_1.cathode, LED2_2.cathode, LED2_3.cathode, RLEDsTop.Pin_1
  N2: LED2_1.anode, U2.D9_(PWM)
  N3: LED2_2.anode, U2.D10_(PWM)
  N4: LED2_3.anode, U2.D11_(PWM)
  N5: RLEDsTop.Pin_0, RLedsMid.Pin_0, RLEDsBottom.Pin_0, U2.GND, C4.1, C5.2, VCC.-
  N6: LED1_1.cathode, LED1_2.cathode, LED1_3.cathode, RLEDsBottom.Pin_1
  N7: LED1_1.anode, U2.D6_(PWM)
  N8: LED1_2.anode, U2.D7
  N9: LED1_3.anode, U2.D8
  N10: LEDM_3.cathode, LEDM_2.cathode, LEDM_1.cathode, RLedsMid.Pin_1
  N11: LEDM_3.anode, U2.A2
  N12: LEDM_2.anode, U2.A1
  N13: LEDM_1.anode, U2.A0
  N14: U2.D2, RSBottom.Pin_0
  N15: U2.D3_(PWM), RHBottom.Pin_0
  N16: U2.D4, RHTop.Pin_0
  N17: U2.VCC, U2.AVCC, U2.AREF, VCC.+
  N18: U2.XLAT1, C4.2, Y2.2
  N19: U2.XLAT2, C5.1, Y2.1
  N20: U2.D5_(PWM), RSTop.Pin_0
  N21: U2.A4, RHMid.Pin_0
  N22: U2.A5, RSMid.Pin_0
  N23: TouchMid1.Pin_1, RHMid.Pin_1, RSMid.Pin_1
  N24: RHTop.Pin_1, RSTop.Pin_1, TouchTop.Pin_1
  N25: RHBottom.Pin_1, RSBottom.Pin_1, TouchBottom.Pin_1

notes:
  Capacitors: 22 pF
  Crystal: 16 MHz
