# Fritzing sketch MysteryMachine (saved by Fritzing 0.8.5b)
circuit board: 16cm x 10cm
breadboards: 3

parts:
  J1 = male pin header, 16 pins [form="♂ (male)"]
  LED1R = LED - 5mm [color="Red (633nm)" package="5 mm [THT]"]
  LED1G = LED - 5mm [color="Green (555nm)" package="5 mm [THT]"]
  LED1B = LED - 5mm [color="Blue (430nm)" package="5 mm [THT]"]
  R1R = Resistor [tolerance=±5% resistance=1k package=THT]
  R1G = Resistor [tolerance=±5% resistance=1k package=THT]
  R1B = Resistor [tolerance=±5% resistance=1k package=THT]
  J2 = male pin header, 16 pins [form="♂ (male)"]
  LED2R = LED - 5mm [color="Red (633nm)" package="5 mm [THT]"]
  LED2G = LED - 5mm [color="Green (555nm)" package="5 mm [THT]"]
  LED2B = LED - 5mm [color="Blue (430nm)" package="5 mm [THT]"]
  R2B = Resistor [tolerance=±5% resistance=1k package=THT]
  R2G = Resistor [tolerance=±5% resistance=1k package=THT]
  R2R = Resistor [tolerance=±5% resistance=1k package=THT]
  LEDL = LED - 5mm [color="Red (633nm)" package="5 mm [THT]"]
  LEDM = LED - 5mm [color="Green (555nm)" package="5 mm [THT]"]
  LEDR = LED - 5mm [color="Blue (430nm)" package="5 mm [THT]"]
  RL = Resistor [tolerance=±5% resistance=1k package=THT]
  RM = Resistor [tolerance=±5% resistance=1k package=THT]
  RR = Resistor [tolerance=±5% resistance=1k package=THT]
  S1 = Pushbutton [package="[THT]"]
  VCC1 = Battery
  S3 = Toggle Switch [package=THT]

nets:
  N1: J1.pin1, LED1R.anode
  N2: J1.pin2, LED1G.anode
  N3: J1.pin3, LED1B.anode
  N4: J1.pin4, J2.pin5
  N5: J1.pin5, J2.pin6
  N6: J1.pin6, J2.pin4
  N7: J1.pin7, J2.pin7
  N8: J1.pin8, J2.pin8
  N9: J1.pin9, J2.pin9
  N10: J1.pin10, J2.pin12
  N11: J1.pin11, J2.pin10
  N12: J1.pin12, J2.pin11
  N13: J1.pin13, J1.pin14, J1.pin15, J1.pin16, J2.pin13, S3.L2
  N14: LED1R.cathode, R1R.Pin_0
  N15: LED1G.cathode, R1G.Pin_0
  N16: LED1B.cathode, R1B.Pin_0
  N17: R1R.Pin_1, R1G.Pin_1, R1B.Pin_1, R2B.Pin_1, R2G.Pin_1, R2R.Pin_1, S1.Pin_1, S1.Pin_2, VCC1.-
  N18: J2.pin1, LED2R.anode
  N19: J2.pin2, LED2G.anode
  N20: J2.pin3, LED2B.anode
  N21: J2.pin14, LEDL.anode
  N22: J2.pin15, LEDM.anode
  N23: J2.pin16, LEDR.anode
  N24: LED2R.cathode, R2R.Pin_0
  N25: LED2G.cathode, R2G.Pin_0
  N26: LED2B.cathode, R2B.Pin_0
  N27: LEDL.cathode, RL.Pin_0
  N28: LEDM.cathode, RM.Pin_0
  N29: LEDR.cathode, RR.Pin_0
  N30: RL.Pin_1, RM.Pin_1, RR.Pin_1, S1.Pin_3, S1.Pin_4
  N31: VCC1.+, S3.COM

notes:
  Rotary switch 1:
  1: LED1R
  2: LED1G
  3: LED1B
  4: Logic 1R
  5: Logic 1G
  6: Logic 1B
  7: Logic 2R
  8: Logic 2G
  9: Logic 2B
  10: Logic 3R
  11: Logic 3G
  12: Logic 3B
  13: pin A: power LED1_x
  14: pin B: power logic 1
  15: pin C: power logic 2
  16: pin D: power logic 3
  Rotary switch 2:
  1: LED2R
  2: LED2G
  3: LED2B
  4: Logic 1R
  5: Logic 1G
  6: Logic 1B
  7: Logic 2R
  8: Logic 2G
  9: Logic 2B
  10: Logic 3R
  11: Logic 3G
  12: Logic 3B
  13: pin A: power LED2x
  14: pin B: ground logic 1
  15: pin C: ground logic 2
  16: pin D: ground logic 3
  1-1: LEDL
  2-2: LEDM
  3-3: LEDR
  Debugging tip:
  Without the rotary switches connected to the headers,
  all pins of the same header should be seperate, except for J1 pins 13-16 (these supply all power)
