# Fritzing sketch MysteryMachineDual (saved by Fritzing 0.8.5b)
circuit board: 16cm x 10cm
breadboards: 3

parts:
  J1 = male pin header, 16 pins [form="♂ (male)"]
  LED1R = LED - 5mm [color="Red (633nm)" package="5 mm [THT]"]
  LED1G = LED - 5mm [color="Green (555nm)" package="5 mm [THT]"]
  LED1B = LED - 5mm [color="Blue (430nm)" package="5 mm [THT]"]
  R1 = Resistor [tolerance=±5% resistance=1k package=THT]
  J2 = male pin header, 16 pins [form="♂ (male)"]
  LED2R = LED - 5mm [color="Red (633nm)" package="5 mm [THT]"]
  LED2G = LED - 5mm [color="Green (555nm)" package="5 mm [THT]"]
  LED2B = LED - 5mm [color="Blue (430nm)" package="5 mm [THT]"]
  R2 = Resistor [tolerance=±5% resistance=1k package=THT]
  LEDL = LED - 5mm [color="Red (633nm)" package="5 mm [THT]"]
  LEDM = LED - 5mm [color="Green (555nm)" package="5 mm [THT]"]
  LEDR = LED - 5mm [color="Blue (430nm)" package="5 mm [THT]"]
  R_C = Resistor [tolerance=±5% resistance=1k package=THT]
  VCC1 = Battery
  Power2 = Toggle Switch [package=THT]
  Power1 = Toggle Switch [package=THT]
  S1 = Pushbutton [package="[THT]"]
  S2 = Pushbutton [package="[THT]"]

nets:
  N1: J1.pin1, LED1R.anode
  N2: J1.pin2, LED1G.anode
  N3: J1.pin3, LED1B.anode
  N4: J1.pin4, J2.pin5
  N5: J1.pin5, J2.pin6
  N6: J1.pin6, J2.pin4
  N7: J1.pin7, J2.pin7
  N8: J1.pin8, J2.pin8
  N9: J1.pin9, J2.pin9
  N10: J1.pin10, J2.pin12
  N11: J1.pin11, J2.pin10
  N12: J1.pin12, J2.pin11
  N13: J1.pin13, J1.pin14, J1.pin15, J1.pin16, J2.pin13, Power2.COM
  N14: LED1R.cathode, LED1G.cathode, LED1B.cathode, R1.Pin_0
  N15: R1.Pin_1, R2.Pin_1, VCC1.-, S2.Pin_1, S2.Pin_2
  N16: J2.pin1, LED2R.anode
  N17: J2.pin2, LED2G.anode
  N18: J2.pin3, LED2B.anode
  N19: J2.pin14, LEDL.anode
  N20: J2.pin15, LEDM.anode
  N21: J2.pin16, LEDR.anode
  N22: LED2R.cathode, LED2G.cathode, LED2B.cathode, R2.Pin_0
  N23: LEDL.cathode, LEDM.cathode, LEDR.cathode, R_C.Pin_0
  N24: R_C.Pin_1, S1.Pin_3, S1.Pin_4
  N25: VCC1.+, Power1.COM
  N26: Power2.L1, Power1.L1
  N27: Power2.L2, Power1.L2
  N28: S1.Pin_1, S1.Pin_2, S2.Pin_3, S2.Pin_4

notes:
  Rotary switch 1:
  1: LED1R
  2: LED1G
  3: LED1B
  4: Logic 1R
  5: Logic 1G
  6: Logic 1B
  7: Logic 2R
  8: Logic 2G
  9: Logic 2B
  10: Logic 3R
  11: Logic 3G
  12: Logic 3B
  13: pin A: power LED1_x
  14: pin B: power logic 1
  15: pin C: power logic 2
  16: pin D: power logic 3
  Rotary switch 2:
  1: LED2R
  2: LED2G
  3: LED2B
  4: Logic 1R
  5: Logic 1G
  6: Logic 1B
  7: Logic 2R
  8: Logic 2G
  9: Logic 2B
  10: Logic 3R
  11: Logic 3G
  12: Logic 3B
  13: pin A: power LED2x
  14: pin B: ground logic 1
  15: pin C: ground logic 2
  16: pin D: ground logic 3
  1-1: LEDL
  2-2: LEDM
  3-3: LEDR
  Debugging tip:
  Without the rotary switches connected to the headers,
  all pins of the same header should be seperate, except for J1 pins 13-16 (these supply all power)
  Hotel switch
  Both sides must push
